# Fritzing sketch smart_glasses_circuit_diagram (saved by Fritzing 0.9.3b)
breadboards: 1

parts:
  Mod1 = ESP32 - CAM
  Part1 = Arduino Nano (Rev3.0) (ICSP)
  Switch = Round Pushbutton
  LED1 = LED - 3mm [color="Red (633nm)" package="3 mm [THT]"]
  R1 = Resistor [tolerance=±5% resistance=220 package=THT]
  VCC2 = Battery
  MP3_Playback_Module = sv5w
  R2 = Resistor [tolerance=±5% resistance=220 package=THT]
  LED2 = LED - 5mm [color="Green (555nm)" package="5 mm [THT]"]

nets:
  5V: Mod1.5V, Part1.5V, MP3_Playback_Module.VCC
  GND: Mod1.GND, Part1.GND, Switch.leg1, VCC2.-, MP3_Playback_Module.GND, MP3_Playback_Module.GND-12
  N1: Mod1.VOT, Part1.D1/TX
  N2: Mod1.VOR, Part1.D0/RX
  N3: Part1.D2, Switch.leg0
  N4: Part1.D8, MP3_Playback_Module.RXD/IO1
  N5: Part1.D9, MP3_Playback_Module.TXD/IO0
  N6: Part1.D11/MOSI, R2.Pin_0
  N7: Part1.D12/MISO, R1.Pin_0
  N8: Part1.VIN, VCC2.+
  N9: LED1.anode, R1.Pin_1
  N10: R2.Pin_1, LED2.anode

notes:
  => to Earphones

custom parts:
  ESP32 - CAM: The ESP32-CAM has a very competitive small-size camera module that can operate independently as a minimum system with a footprint of only 27*40.5*4.5mm and a deep sleep current of up to 6mA.
  Battery: Your standard 2x 18650 battery pack (14.7 Volts)
  sv5w: DY-SV5W is an intelligent voice module. It integrates I/O subsection triggering, UART serial port control, ONE_line single bus serial port control3. Onboard 5W Class D amplifier circuit and can directly drive 4ohm 3~5W speakers. Support MP3,WAV decoding format. Max support 32Gbit(4MByte) TF card memory, can connect the computer to update TF card to store audio files via USB cable.
